# Fritzing sketch Diagrama - Display e DHT11 (saved by Fritzing 1.0.4)
breadboards: 1

parts:
  OLED_I2C1 = OLED 128x64 I2C Monochrome Display
  DHT1 = DHT11 Humitidy and Temperature Sensor
  Componente1 = BlackBoard v1.1

nets:
  N1: OLED_I2C1.SDA, Componente1.A4/SDA
  N2: OLED_I2C1.SCK, Componente1.A5/SCL
  VDD: OLED_I2C1.VDD, Componente1.3V3
  GND: OLED_I2C1.GND, DHT1.GND, Componente1.GND
  VDD_2: DHT1.VDD, Componente1.5V
  N3: DHT1.DATA, Componente1.A1

custom parts:
  DHT11 Humitidy and Temperature Sensor: DHT11 Humidity and Temperature Sensor
  BlackBoard v1.1: Esta é a BlackBoard, a placa Arduino compatível fabricada pela RoboCore. Ela foi projetada unindo o melhor das placas Arduino básicas lançadas até hoje, além de algumas melhorias feitas pelos nossos engenheiros. Veja abaixo as vantagens desta placa para a Arduino UNO R3: Suporta maior drenagem de corrente elétrica em seu pino de 5V (suporta um maior número de periféricos ligados a ela, sem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
